# Fritzing sketch terrarium-esp8266 (saved by Fritzing 0.9.4)
breadboards: 1

parts:
  U1 = NodeMCU V1.0
  Part1 = Soil Moisture Sensor
  J1 = Screw terminal - 2 pins [package=THT]
  J2 = Screw terminal - 2 pins [package=THT]
  Q1 = NPN-Transistor [package="TO92 [THT]"]
  DHT1 = DHT11 Humitidy and Temperature Sensor

nets:
  GND: U1.GND, Part1.GND, J1.pin2, Q1.C, DHT1.GND
  N1: U1.D5, Q1.B
  N2: U1.D6, DHT1.DATA
  VIN: U1.Vin, Part1.VCC, J1.pin1, J2.pin1, DHT1.VDD
  N3: U1.A0, Part1.SIG
  N4: J2.pin2, Q1.E

custom parts:
  NodeMCU V1.0: ESP8266 based NodeMCU
  DHT11 Humitidy and Temperature Sensor: DHT11 Humidity and Temperature Sensor
